// Logisim project Mikroprozessor_A_8_v0.1.circ as structural Verilog: 1 circuit, main circuit main
module main (
);

  wire Ain, ALo, Bin, button_1_out, Cin, CLK, clock_1_out, Cot, Fin, HLT, LDC, Mot, not_1_out, RAi, Rin, Rot;
  wire [7:0] adder_1_out, controlled_buffer_1_out, register_1_q, register_2_q, register_3_q, register_4_q,
       register_5_q, register_6_q, subtractor_1_out;
  wire [8:0] counter_1_q_2, undriven;
  wire [8:1] counter_1_q;
  wire [15:8] rom_1_data;

  Button button_1 (.out(button_1_out));
  Counter #(.max('h1ff), .width(9)) counter_1 (
    .clr(button_1_out), .load(LDC), .clk(CLK), .D(undriven), .Q({counter_1_q, counter_1_q_2[0]}));  // open: up, count, carry
  Clock clock_1 (.out(clock_1_out));
  Register register_1 (.D(undriven[8:1]), .en(Ain), .clk(CLK), .Q(register_1_q));  // open: clr
  Register register_2 (.D(undriven[8:1]), .en(Bin), .clk(CLK), .Q(register_2_q));  // open: clr
  xor xor_1 (CLK, clock_1_out, HLT);
  Register register_3 (.D(undriven[8:1]), .en(Fin), .clk(CLK), .Q(register_3_q));  // open: clr
  Adder adder_1 (.a(register_1_q), .b(register_2_q), .out(adder_1_out));  // open: cin, cout
  Subtractor subtractor_1 (.a(register_1_q), .b(register_2_q), .out(subtractor_1_out));  // open: bin, bout
  assign controlled_buffer_1_out = register_3_q[0] ? adder_1_out : 8'bz;  // Controlled_Buffer controlled_buffer_1
  assign controlled_buffer_1_out = register_3_q[1] ? subtractor_1_out : 8'bz;  // Controlled_Buffer controlled_buffer_2
  Register register_4 (.D(controlled_buffer_1_out), .en(1'b1), .clk(CLK), .Q(register_4_q));  // open: clr
  ROM #(.dataWidth(16)) rom_1 (.addr(counter_1_q), .data({rom_1_data, counter_1_q_2[8:1]}));
  assign undriven[8:1] = ALo ? register_4_q : 8'bz;  // Controlled_Buffer controlled_buffer_3
  Register register_5 (.D(undriven[8:1]), .en(Cin), .clk(CLK), .Q(register_5_q));  // open: clr
  assign undriven[8:1] = Cot ? register_5_q : 8'bz;  // Controlled_Buffer controlled_buffer_4
  Register register_6 (.D(undriven[8:1]), .en(RAi), .clk(CLK), .Q(register_6_q));  // open: clr
  RAM ram_1 (.addr(register_6_q), .we(Rin), .oe(not_1_out), .clk(CLK), .din(undriven[8:1]), .dout(undriven[8:1]));
  not not_1 (not_1_out, Rot);
  assign undriven[8:1] = Mot ? rom_1_data : 8'bz;  // Controlled_Buffer controlled_buffer_5
  ROM #(.addrWidth(9), .dataWidth(12)) rom_2 (
    .addr(counter_1_q_2), .data({ALo, Fin, Rot, Rin, RAi, Mot, Cot, Cin, Bin, Ain, HLT, LDC}));

  // Notes on the sheet:
  //   contents of rom_1 (hex, n*v repeats v):
  //   ff
  //   contents of rom_2 (hex, n*v repeats v):
  //   fff
endmodule
